# Fritzing sketch Smart_Room_Controller (saved by Fritzing 0.9.4)
breadboards: 3

parts:
  Breadboard4 = Breadboard Split Power
  Breadboard5 = Breadboard Split Power
  Teensy_3_1 = Teensy 3.1
  M1 = BMP280
  Part1 = 12 NeoPixel Ring [part_number=1643]
  S1 = Pushbutton [package="[THT]"]
  S2 = Pushbutton [package="[THT]"]
  RG_encoder1 = SprkFn RG Encoder [package="DIP (Dual Inline) [THT]"]
  OLED_I2C1 = OLED 128x64 I2C Monochrome Display
  WIZ820io1 = WIZ820io [part_number=WIZ820io]
  R1 = Resistor [tolerance=±5% resistance=220 package=THT]
  R2 = Resistor [tolerance=±5% resistance=220 package=THT]
  HC-SR04_Sensor_1 = HC-SR04 Ultrasonic Distance Sensor

nets:
  N1: Breadboard4.pin15Y, Breadboard4.pin17Y, Breadboard4.pin29Y, Breadboard5.pin3Y, Breadboard5.pin15Y, Breadboard5.pin17Y
  N2: Breadboard4.pin29Z, Breadboard5.pin3Z
  GND: Teensy_3_1.GND, HC-SR04_Sensor_1.GND
  N3: Teensy_3_1.D9, WIZ820io1.nRESET
  N4: Teensy_3_1.D10, WIZ820io1.nSS
  N5: Teensy_3_1.D11, WIZ820io1.MOSI
  N6: Teensy_3_1.D12, WIZ820io1.MISO
  N7: Teensy_3_1.A0/D14, S2.Pin_1, S2.Pin_2, R2.Pin_0
  N8: Teensy_3_1.A1/D15, S1.Pin_1, S1.Pin_2, R1.Pin_0
  N9: Teensy_3_1.A3/D17, RG_encoder1.+G
  N10: Teensy_3_1.A4/D18, M1.SDA, OLED_I2C1.SDA
  N11: Teensy_3_1.A5/D19, M1.SCL, OLED_I2C1.SCK
  N12: Teensy_3_1.A6/D20, RG_encoder1.SW
  N13: Teensy_3_1.A7/D21, Part1.IN
  N14: Teensy_3_1.A8/D22, RG_encoder1.A
  N15: Teensy_3_1.A9/D23, RG_encoder1.C
  VIN: Teensy_3_1.Vin, M1.VIN, Part1.VDD, S1.Pin_3, S1.Pin_4, S2.Pin_3, S2.Pin_4, OLED_I2C1.VDD
  GND_2: M1.GND, OLED_I2C1.GND
  N16: Part1.GND, RG_encoder1.B, R1.Pin_1, R2.Pin_1
  VIN_2: WIZ820io1.VIN, HC-SR04_Sensor_1.VCC

custom parts:
  Breadboard Split Power: A custom 6 pin per group power supply strip where the top row (ground) is all bussed together and the bottom row (+V) is split in two groups of 12 pins. This version is modified to be a loadable part and was rescaled to be on the standard 1px = 1thou grid with the size set in inches
  BMP280: Temperature Humidity Barometric presure Sensor, I2C
  12 NeoPixel Ring: 12 ultra bright smart LED NeoPixels are arranged in a circle with 1.5" (37mm) outer diameter. The rings are 'chainable' - connect the output pin of one to the input pin of another. Use only one microcontroller pin to control as many as you can chain together! Each LED is addressable as the driver chip is inside the LED. Each one has ~18mA constant current drive so the color will be very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
  Pushbutton: A generic pushbutton.
  SprkFn RG Encoder: SparkFun RG Rotary Encoder
